# Fritzing sketch beerduino (saved by Fritzing 0.6.5b)
breadboards: 1

parts:
  Arduino2 = Arduino
  R3 = Resistor [resistance=1k tolerance=±5% package=THT]
  T1 = LM35 Temperature Sensor [package="TO92 [THT]"]
  T3 = LM35 Temperature Sensor [package="TO92 [THT]"]

nets:
  N1: Arduino2.D2, R3.Pin_0, T1.Vout
  N2: Arduino2.+5V, R3.Pin_1
  GND: Arduino2.GND, T1.+Vs, T1.GND, T3.+Vs, T3.GND
